// Logisim project cpu.circ as structural Verilog: 5 circuits, main circuit CPU
module CPU (
  output [7:0] PC
);

  wire clock_1_out;
  wire [1:0] instruction_decoder_1_rd, instruction_decoder_1_rs, instruction_decoder_1_rt, multiplexer_1_out;
  wire [7:0] alu_1_output, instruction_decoder_1_immediate, multiplexer_2_out, register_file_1_read_data_1,
       register_file_1_read_data_2;
  wire [15:0] rom_1_data;

  Clock clock_1 (.out(clock_1_out));
  PC pc_1 (.Output(PC), .Clock(clock_1_out));
  Instruction_Decoder instruction_decoder_1 (
    .Instruction(rom_1_data), .RS(instruction_decoder_1_rs), .RT(instruction_decoder_1_rt),
    .RD(instruction_decoder_1_rd), .Immediate(instruction_decoder_1_immediate));  // open: Opcode
  ROM #(.dataWidth(16)) rom_1 (.addr(PC), .data(rom_1_data));  // open: sel
  Multiplexer #(.width(2), .enable("false")) multiplexer_1 (
    .in0(instruction_decoder_1_rt), .in1(instruction_decoder_1_rd), .out(multiplexer_1_out));  // open: sel
  Register_File register_file_1 (
    .Write_Data(alu_1_output), .Read_Data_1(register_file_1_read_data_1),
    .Read_Register_1(instruction_decoder_1_rs), .Read_Data_2(register_file_1_read_data_2),
    .Read_Register_2(instruction_decoder_1_rt), .Write_Address(multiplexer_1_out));  // open: Write_Enable, Clock
  Multiplexer #(.width(8), .enable("false")) multiplexer_2 (
    .in0(register_file_1_read_data_2), .in1(instruction_decoder_1_immediate), .out(multiplexer_2_out));  // open: sel
  ALU alu_1 (
    .Data_A(register_file_1_read_data_1), .Data_B(multiplexer_2_out), .Output(alu_1_output));  // open: Branch, Zero_Dectector, Select
  RAM #(.bus("separate")) ram_1 (.addr(alu_1_output), .din(multiplexer_2_out));  // open: data, str, sel, clk, ld, clr
endmodule

module Instruction_Decoder (
  input  [15:0] Instruction,
  output [3:0] Opcode,
  output [1:0] RS,
  output [1:0] RT,
  output [1:0] RD,
  output [7:0] Immediate
);


  assign Immediate = Instruction[7:0];
  assign Opcode = Instruction[15:12];
  assign RD = Instruction[7:6];
  assign RS = Instruction[11:10];
  assign RT = Instruction[9:8];
endmodule

module Register_File (
  input  [7:0] Write_Data,
  input  Clock,
  input  Write_Enable,
  input  [1:0] Read_Register_1,
  input  [1:0] Write_Address,
  input  [1:0] Read_Register_2,
  output [7:0] Read_Data_1,
  output [7:0] Read_Data_2
);

  wire and_1_out, and_2_out, and_3_out, and_4_out, decoder_1_out0, decoder_1_out1, decoder_1_out2,
       decoder_1_out3;
  wire [7:0] R0_q, R1_q, R2_q, R3_q;

  Decoder #(.select(2)) decoder_1 (
    .out0(decoder_1_out0), .out1(decoder_1_out1), .out2(decoder_1_out2), .out3(decoder_1_out3),
    .sel(Write_Address));  // open: en
  and and_1 (and_1_out, Write_Enable, decoder_1_out0);
  and and_2 (and_2_out, Write_Enable, decoder_1_out1);
  and and_3 (and_3_out, Write_Enable, decoder_1_out2);
  and and_4 (and_4_out, Write_Enable, decoder_1_out3);
  Register R0 (.D(Write_Data), .en(and_1_out), .Q(R0_q), .clk(Clock));  // open: clr
  Register R1 (.D(Write_Data), .en(and_2_out), .Q(R1_q), .clk(Clock));  // open: clr
  Register R2 (.D(Write_Data), .en(and_3_out), .Q(R2_q), .clk(Clock));  // open: clr
  Register R3 (.D(Write_Data), .en(and_4_out), .Q(R3_q), .clk(Clock));  // open: clr
  Multiplexer #(.select(2), .width(8)) multiplexer_1 (
    .in0(R0_q), .in1(R1_q), .in2(R2_q), .in3(R3_q), .out(Read_Data_1), .sel(Read_Register_1));  // open: en
  Multiplexer #(.select(2), .width(8)) multiplexer_2 (
    .in0(R0_q), .in1(R1_q), .in2(R2_q), .in3(R3_q), .out(Read_Data_2), .sel(Read_Register_2));  // open: en
endmodule

module ALU (
  input  [7:0] Data_A,
  input  [1:0] Select,
  input  [7:0] Data_B,
  output [7:0] Output,
  output Branch,
  output Zero_Dectector
);

  wire comparator_1_gt, comparator_1_lt, not_1_out;
  wire [7:0] adder_1_out, bit_extender_1_out, subtractor_1_out, xor_1_out;

  assign xor_1_out = Data_A ^ Data_B;  // XOR_Gate xor_1, 8 bits wide
  Adder adder_1 (.a(Data_A), .b(Data_B), .out(adder_1_out));  // open: cin, cout
  Subtractor subtractor_1 (.a(Data_A), .b(Data_B), .out(subtractor_1_out));  // open: bin, bout
  Comparator comparator_1 (.a(Data_A), .b({8{1'b0}}), .gt(comparator_1_gt), .eq(Zero_Dectector), .lt(comparator_1_lt));
  assign bit_extender_1_out = {{7{1'b0}}, comparator_1_lt};  // Bit_Extender bit_extender_1
  Multiplexer #(.select(2), .width(8), .enable("false")) multiplexer_1 (
    .in0(xor_1_out), .in1(adder_1_out), .in2(subtractor_1_out), .in3(bit_extender_1_out), .out(Output),
    .sel(Select));
  not not_1 (not_1_out, Zero_Dectector);
  Multiplexer #(.select(2), .enable("false")) multiplexer_2 (
    .in0(comparator_1_gt), .in1(Zero_Dectector), .in2(comparator_1_lt), .in3(not_1_out), .out(Branch),
    .sel(Select));
endmodule

module PC (
  input  Clock,
  output [7:0] Output
);

  wire [7:0] adder_1_out;

  Adder adder_1 (.a(Output), .b(8'h2), .out(adder_1_out));  // open: cin, cout
  Register register_1 (.D(adder_1_out), .Q(Output), .clk(Clock));  // open: en, clr
endmodule
